# Fritzing sketch RGB (saved by Fritzing 0.9.5d)
breadboards: 1

parts:
  Part1 = Maker Uno (Arduino Uno Compatible)
  LED1 = RGB LED (com. cathode, rgb) [package="5 mm [THT]"]

nets:
  N1: Part1.GND, LED1.green_anode

custom parts:
  Maker Uno (Arduino Uno Compatible): Maker Uno, an Arduino UNO compatible board designed and developed specially for students to learn coding and microcontroller. We named it Maker UNO to encourage everyone to be a maker by getting started with this amazing board. Oh! BTW, it is PURPLE color.
  RGB LED (com. cathode, rgb): A 5mm tri-color LED with red, green and blue inside.
