# Fritzing sketch Water level (saved by Fritzing 0.9.5d)
breadboards: 1

parts:
  Part1 = Maker Uno (Arduino Uno Compatible)
  Water_Level_Sensor1 = Water Level Sensor

nets:
  N1: Part1.A2, Water_Level_Sensor1.SIG
  5V: Part1.5V, Water_Level_Sensor1.VCC
  GND: Part1.GND, Water_Level_Sensor1.GND

custom parts:
  Maker Uno (Arduino Uno Compatible): Maker Uno, an Arduino UNO compatible board designed and developed specially for students to learn coding and microcontroller. We named it Maker UNO to encourage everyone to be a maker by getting started with this amazing board. Oh! BTW, it is PURPLE color.
  Water Level Sensor: A water level sensor. This sensor operates at 3V to 5V. The Sig (signal) pin outputs an analogue signal that is in proportion to the amount of water in contact with the sensor.
